# Fritzing sketch Untitled Sketch (saved by Fritzing 0.9.3b)
breadboards: 2

parts:
  Componente1 = Arduino Uno (Rev3)
  Componente2 = Rotoshield - Motor driver shield for Arduino
  Componente3 = Bluetooth HC-05 Macho
  M2 = DC Motor
  M1 = DC Motor

nets:
  N1: Componente1.D8, Componente2.DIG_8
  N2: Componente1.D9_PWM, Componente2.DIG_9
  N3: Componente1.D10_PWM/SS, Componente2.DIG_10
  N4: Componente1.D11_PWM/MOSI, Componente2.DIG_11
  N5: Componente1.D12/MISO, Componente2.DIG_12
  N6: Componente1.D13/SCK, Componente3.TXD
  GND: Componente1.GND, Componente2.GND, Componente3.GND
  N7: Componente1.AREF, Componente2.AREF
  N8: Componente1.D0/RX, Componente2.DIG_0
  N9: Componente1.D1/TX, Componente2.DIG_1
  N10: Componente1.D3_PWM, Componente2.DIG_3
  N11: Componente1.D4, Componente2.DIG_4
  N12: Componente1.D5_PWM, Componente2.DIG_5
  N13: Componente1.D6_PWM, Componente2.DIG_6
  N14: Componente1.D7, Componente2.DIG_7
  N15: Componente1.RESET, Componente2.RESET
  3V3: Componente1.3V3, Componente2.+3V3
  5V: Componente1.5V, Componente2.+5V, Componente3.VCC
  VIN: Componente1.VIN, Componente2.VIN
  N16: Componente2.DIG_2, Componente3.RXD
  N17: Componente2.M3-2, M1.pin_2
  N18: Componente2.M3-1, M1.pin_1
  N19: Componente2.M4-2, M2.pin_2
  N20: Componente2.M4-1, M2.pin_1
